// Logisim project Processador.circ as structural Verilog: 4 circuits, main circuit main
module main (
);

  wire Clk, d_breg, dmx_imm, MULA, multiplexer_2_out, WBReg, wm;
  wire [3:0] opcode, rom_1_data_3, Rs1_2;
  wire [7:0] rom_1_data_2;
  wire [7:4] rom_1_data;
  wire [11:0] demultiplexer_1_out0;
  wire [11:4] demultiplexer_1_out1;
  wire [19:0] bancoderegistradores_1_b, data, Imm8, Imm12, multiplexer_1_out, multiplexer_3_out,
       multiplexer_4_out, PC_1, PC_B, PC_J, PC_q, Ra, ram_1_dout, ula_1_s;

  Multiplexer #(.width(20)) multiplexer_1 (.in0(PC_B), .in1(PC_1), .out(multiplexer_1_out), .sel(multiplexer_2_out));
  Multiplexer #(.select(2)) multiplexer_2 (.out(multiplexer_2_out));  // open: in0, in1, in2, in3, sel
  Clock clock_1 (.out(Clk));
  Register #(.width(20)) PC (.D(multiplexer_3_out), .en(1'b1), .clk(Clk), .Q(PC_q));  // open: clr
  Multiplexer #(.select(2), .width(20)) multiplexer_3 (
    .in0(PC_1), .in1(multiplexer_1_out), .in2(PC_J), .in3(data), .out(multiplexer_3_out));  // open: sel
  Adder #(.width(20)) adder_1 (.a(PC_q), .b(20'h1), .out(PC_1));  // open: cin, cout
  Adder #(.width(20)) adder_2 (.a(PC_q), .b(Imm12), .out(PC_J));  // open: cin, cout
  Adder #(.width(20)) adder_3 (.a(PC_q), .b(Imm8), .out(PC_B));  // open: cin, cout
  ROM #(.addrWidth(20), .dataWidth(20)) rom_1 (.addr(PC_q), .data({rom_1_data_3, rom_1_data_2, rom_1_data, opcode}));
  Demultiplexer #(.width(12)) demultiplexer_1 (
    .out0(demultiplexer_1_out0), .out1({demultiplexer_1_out1, Rs1_2}), .in({rom_1_data_3, rom_1_data_2}),
    .sel(dmx_imm));
  assign Imm12 = {{8{demultiplexer_1_out0[11]}}, demultiplexer_1_out0};  // Bit_Extender bit_extender_1
  assign Imm8 = {{12{demultiplexer_1_out1[11]}}, demultiplexer_1_out1};  // Bit_Extender bit_extender_2
  ROM #(.addrWidth(4), .dataWidth(20)) rom_2 (.addr(opcode));  // open: data
  VerificadorBranch verificadorbranch_1 (.rs1(Rs1_2), .rs2(rom_1_data));  // open: Is_NE, Is_EQ, Is_GE, Is_LT
  BancoDeRegistradores bancoderegistradores_1 (
    .DADO(data), .rs1(rom_1_data), .rs2(rom_1_data_2[3:0]), .rd(rom_1_data_2[7:4]), .clk(Clk), .W(WBReg),
    .A(Ra), .B(bancoderegistradores_1_b));
  Multiplexer #(.width(20)) multiplexer_4 (
    .in0(bancoderegistradores_1_b), .in1(Imm8), .out(multiplexer_4_out), .sel(MULA));
  Multiplexer #(.width(20)) multiplexer_5 (.in0(ram_1_dout), .in1(ula_1_s), .out(data), .sel(d_breg));
  ULA ula_1 (.A(Ra), .B(multiplexer_4_out), .Funct(rom_1_data_3), .S(ula_1_s));
  RAM #(.addrWidth(20), .dataWidth(20)) ram_1 (
    .addr(bancoderegistradores_1_b), .we(wm), .oe(1'b1), .clk(Clk), .din(Ra), .dout(ram_1_dout));
endmodule

module BancoDeRegistradores (
  input  [19:0] DADO,
  input  [3:0] rs1,
  input  [3:0] rs2,
  input  [3:0] rd,
  input  clk,
  input  W,
  output [19:0] A,
  output [19:0] B
);

  wire w00, w01, w02, w03, w04, w05, w06, w07, w08, w09, w10, w11, w12, w13, w14, w15;
  wire [19:0] vr01, vr02, vr03, vr04, vr05, vr06, vr07, vr08, vr09, vr10, vr11, vr12, vr13, vr14, vr15;

  Register #(.width(20)) R01 (.D(DADO), .en(w01), .clk(clk), .Q(vr01));  // open: clr
  Register #(.width(20)) R02 (.D(DADO), .en(w02), .clk(clk), .Q(vr02));  // open: clr
  Register #(.width(20)) R03 (.D(DADO), .en(w03), .clk(clk), .Q(vr03));  // open: clr
  Register #(.width(20)) R04 (.D(DADO), .en(w04), .clk(clk), .Q(vr04));  // open: clr
  Register #(.width(20)) R05 (.D(DADO), .en(w05), .clk(clk), .Q(vr05));  // open: clr
  Register #(.width(20)) R06 (.D(DADO), .en(w06), .clk(clk), .Q(vr06));  // open: clr
  Register #(.width(20)) R07 (.D(DADO), .en(w07), .clk(clk), .Q(vr07));  // open: clr
  Register #(.width(20)) R08 (.D(DADO), .en(w08), .clk(clk), .Q(vr08));  // open: clr
  Register #(.width(20)) R09 (.D(DADO), .en(w09), .clk(clk), .Q(vr09));  // open: clr
  Register #(.width(20)) R10 (.D(DADO), .en(w10), .clk(clk), .Q(vr10));  // open: clr
  Register #(.width(20)) R11 (.D(DADO), .en(w11), .clk(clk), .Q(vr11));  // open: clr
  Register #(.width(20)) R12 (.D(DADO), .en(w12), .clk(clk), .Q(vr12));  // open: clr
  Register #(.width(20)) R13 (.D(DADO), .en(w13), .clk(clk), .Q(vr13));  // open: clr
  Register #(.width(20)) R14 (.D(DADO), .en(w14), .clk(clk), .Q(vr14));  // open: clr
  Register #(.width(20)) R15 (.D(DADO), .en(w15), .clk(clk), .Q(vr15));  // open: clr
  Demultiplexer #(.select(4)) demultiplexer_1 (
    .out0(w00), .out1(w01), .out2(w02), .out3(w03), .out4(w04), .out5(w05), .out6(w06), .out7(w07),
    .out8(w08), .out9(w09), .out10(w10), .out11(w11), .out12(w12), .out13(w13), .out14(w14), .out15(w15),
    .in(W), .sel(rd));
  Multiplexer #(.select(4), .width(20)) multiplexer_1 (
    .in0({20{1'b0}}), .in1(vr01), .in2(vr02), .in3(vr03), .in4(vr04), .in5(vr05), .in6(vr06), .in7(vr07),
    .in8(vr08), .in9(vr09), .in10(vr10), .in11(vr11), .in12(vr12), .in13(vr13), .in14(vr14), .in15(vr15),
    .out(A), .sel(rs1));
  Multiplexer #(.select(4), .width(20)) multiplexer_2 (
    .in0({20{1'b0}}), .in1(vr01), .in2(vr02), .in3(vr03), .in4(vr04), .in5(vr05), .in6(vr06), .in7(vr07),
    .in8(vr08), .in9(vr09), .in10(vr10), .in11(vr11), .in12(vr12), .in13(vr13), .in14(vr14), .in15(vr15),
    .out(B), .sel(rs2));

  // Other names for the same wires on the sheet: WD[19:0] = DADO
endmodule

module ULA (
  input  [19:0] A,
  input  [19:0] B,
  input  [3:0] Funct,
  output [19:0] S
);

  wire [19:0] adder_1_out, and_1_out, divider_1_out, divider_1_rem, multiplier_1_out, not_1_out, or_1_out,
       shifter_1_out, shifter_2_out, shifter_3_out, subtractor_1_out, undriven, xor_1_out;

  Adder #(.width(20)) adder_1 (.a(A), .b(B), .out(adder_1_out));  // open: cin, cout
  Subtractor #(.width(20)) subtractor_1 (.a(A), .b(B), .out(subtractor_1_out));  // open: bin, bout
  Multiplier #(.mode("twosComplement"), .width(20)) multiplier_1 (
    .a(A), .b(B), .out(multiplier_1_out));  // open: cin, cout
  Divider #(.mode("twosComplement"), .width(20)) divider_1 (
    .a(A), .b(B), .out(divider_1_out), .rem(divider_1_rem));  // open: upper
  assign or_1_out = A | B;  // OR_Gate or_1, 20 bits wide
  assign and_1_out = A & B;  // AND_Gate and_1, 20 bits wide
  Shifter #(.width(20)) shifter_1 (.in(A), .\dist (B[4:0]), .out(shifter_1_out));
  Shifter #(.shift("lr"), .width(20)) shifter_2 (.in(A), .\dist (B[4:0]), .out(shifter_2_out));
  Shifter #(.shift("ar"), .width(20)) shifter_3 (.in(A), .\dist (B[4:0]), .out(shifter_3_out));
  assign xor_1_out = A ^ B;  // XOR_Gate xor_1, 20 bits wide
  assign not_1_out = ~A;  // NOT_Gate not_1, 20 bits wide
  Multiplexer #(.select(4), .width(20)) multiplexer_1 (
    .in0(adder_1_out), .in1(subtractor_1_out), .in2(multiplier_1_out), .in3(divider_1_out),
    .in4(divider_1_rem), .in5(or_1_out), .in6(and_1_out), .in7(xor_1_out), .in8(not_1_out),
    .in9(shifter_1_out), .in10(shifter_2_out), .in11(shifter_3_out), .in12(undriven), .out(S), .sel(Funct));  // open: in13, in14, in15
endmodule

module VerificadorBranch (
  input  [3:0] rs1,
  input  [3:0] rs2,
  output Is_NE,
  output Is_EQ,
  output Is_GE,
  output Is_LT
);

  Comparator #(.width(4)) comparator_1 (.a(rs1), .b(rs2), .eq(Is_EQ), .lt(Is_LT));  // open: gt
  not not_1 (Is_NE, Is_EQ);
  not not_2 (Is_GE, Is_LT);
endmodule
